# Fritzing sketch Stepper_Fritzing_V1 (saved by Fritzing 0.8.7b)

parts:
  L298N1 = L298N DC motor driver
  BAT1 = 12 battery [package=battery]  # not connected
  WeMos_D1_Mini1 = WeMos D1 Mini
  M1 = Stepper Motor - Bipolar

nets:
  N1: L298N1.OUT1, M1.A
  N2: L298N1.OUT2, M1.C
  N3: L298N1.OUT3, M1.D
  N4: L298N1.OUT4, M1.B
  N5: L298N1.5V#9, L298N1.ENA
  N6: L298N1.5V#10, L298N1.ENB
  N7: L298N1.IN1, WeMos_D1_Mini1.D8
  N8: L298N1.IN2, WeMos_D1_Mini1.D7
  N9: L298N1.IN3, WeMos_D1_Mini1.D6
  N10: L298N1.IN4, WeMos_D1_Mini1.D5

custom parts:
  L298N DC motor driver: 2x DC motor driver with 78M05 positive voltage regulator (7..35 V) L298N: max 46 V, 2 A Set 5 V Enable jumper to enable 5 V regultor (needed for the L298N) and +5 V output at screw terminal or supply external +5 V at screw terminal Set ENA and/or ENB to +5 V to enable motor permanently or supply ENA and/or ENB with PWM signal IN1 and IN2 set rotation directory for motor A (OUT1/OUT2) IN2 and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
  12 battery: 12V lead acid type battery, like the Husqvarna YTH2448 12V 35AH battery. This is the mini version 1/4 the size of the actual battery to be closer to typical breadboard parts (around 2in wide rathher than 7in). The pads in pcb are sized to accomidate up to 14ga wire (as these batterys will deliver high currents.)
  WeMos D1 Mini: The D1 mini is a mini wifi board based on ESP-8266EX.
